# Fritzing sketch hc05 (saved by Fritzing 0.9.3b)

parts:
  Componente1 = Arduino Uno (Rev3)
  Componente2 = Bluetooth HC-05 Macho

nets:
  N1: Componente1.D10_PWM/SS, Componente2.RXD
  N2: Componente1.D11_PWM/MOSI, Componente2.TXD
  5V: Componente1.5V, Componente2.VCC
  GND: Componente1.GND, Componente2.GND
